// Logisim project Digital Vending Machine.circ as structural Verilog: 11 circuits, main circuit Digital Vending Machine
module Digital_Vending_Machine_Circuit (
  input  _1,
  input  _2,
  input  _5,
  input  _10,
  input  Cancel,
  input  Take,
  input  A__2,
  input  B__3,
  input  C__6,
  input  D__8,
  input  E__12,
  input  Restock_A,
  input  Restock_B,
  input  Restock_C,
  input  Restock_D,
  input  Restock_E,
  output out_17,
  output out_18,
  output out_19,
  output out_20,
  output out_21,
  output out_22,
  output out_23,
  output out_24,
  output out_25,
  output out_26,
  output out_27,
  output out_28,
  output out_29,
  output out_30,
  output out_31,
  output out_32,
  output out_33,
  output out_34,
  output out_35,
  output out_36,
  output out_37,
  output out_38,
  output out_39,
  output out_40,
  output out_41,
  output out_42,
  output out_43,
  output out_44,
  output out_45,
  output out_46,
  output out_47,
  output out_48,
  output out_49,
  output out_50,
  output out_51,
  output out_52
);

  wire and_1_out, and_2_out, and_3_out, and_4_out, and_5_out, and_6_out, and_7_out, calculation_1_out_9,
       calculation_1_out_10, calculation_1_out_11, calculation_1_out_12, calculation_1_out_13,
       display_product_1_p2, display_product_1_p5, display_product_1_p7, display_product_1_p10,
       display_product_1_p12, display_product_1_p14, insert_money_1_out_7, insert_money_1_out_8,
       insert_money_1_out_9, insert_money_1_out_10, n4_bit_asynchronous_down_counter_1_out_4,
       n4_bit_asynchronous_down_counter_1_out_5, n4_bit_asynchronous_down_counter_1_out_6,
       n4_bit_asynchronous_down_counter_1_out_7, n4_bit_asynchronous_down_counter_1_out_8,
       n4_bit_asynchronous_down_counter_2_out_4, n4_bit_asynchronous_down_counter_2_out_5,
       n4_bit_asynchronous_down_counter_2_out_6, n4_bit_asynchronous_down_counter_2_out_7,
       n4_bit_asynchronous_down_counter_2_out_8, n4_bit_asynchronous_down_counter_3_out_4,
       n4_bit_asynchronous_down_counter_3_out_5, n4_bit_asynchronous_down_counter_3_out_6,
       n4_bit_asynchronous_down_counter_3_out_7, n4_bit_asynchronous_down_counter_3_out_8,
       n4_bit_asynchronous_down_counter_4_out_4, n4_bit_asynchronous_down_counter_4_out_5,
       n4_bit_asynchronous_down_counter_4_out_6, n4_bit_asynchronous_down_counter_4_out_7,
       n4_bit_asynchronous_down_counter_4_out_8, n4_bit_asynchronous_down_counter_5_out_4,
       n4_bit_asynchronous_down_counter_5_out_5, n4_bit_asynchronous_down_counter_5_out_6,
       n4_bit_asynchronous_down_counter_5_out_7, n4_bit_asynchronous_down_counter_5_out_8, not_1_out,
       not_2_out, or_1_out, or_2_out, product_selection_1_out_8, product_selection_1_out_9,
       product_selection_1_out_10, product_selection_1_out_11;

  and and_1 (and_1_out, not_2_out, Cancel);
  and and_2 (and_2_out, A__2, n4_bit_asynchronous_down_counter_1_out_8);
  _4_bit_Asynchronous_Down_Counter u_4_bit_asynchronous_down_counter_1 (
    .Clock(and_3_out), .Preset(Restock_A), .out_4(n4_bit_asynchronous_down_counter_1_out_4),
    .out_5(n4_bit_asynchronous_down_counter_1_out_5), .out_6(n4_bit_asynchronous_down_counter_1_out_6),
    .out_7(n4_bit_asynchronous_down_counter_1_out_7), .out_8(n4_bit_asynchronous_down_counter_1_out_8),
    .Disable(display_product_1_p12));
  and and_3 (and_3_out, display_product_1_p14, Take);
  and and_4 (and_4_out, B__3, n4_bit_asynchronous_down_counter_2_out_8);
  _4_bit_Asynchronous_Down_Counter u_4_bit_asynchronous_down_counter_2 (
    .Clock(and_3_out), .Preset(Restock_B), .out_4(n4_bit_asynchronous_down_counter_2_out_4),
    .out_5(n4_bit_asynchronous_down_counter_2_out_5), .out_6(n4_bit_asynchronous_down_counter_2_out_6),
    .out_7(n4_bit_asynchronous_down_counter_2_out_7), .out_8(n4_bit_asynchronous_down_counter_2_out_8),
    .Disable(display_product_1_p10));
  _4_bit_Asynchronous_Down_Counter u_4_bit_asynchronous_down_counter_3 (
    .Clock(and_3_out), .Preset(Restock_C), .out_4(n4_bit_asynchronous_down_counter_3_out_4),
    .out_5(n4_bit_asynchronous_down_counter_3_out_5), .out_6(n4_bit_asynchronous_down_counter_3_out_6),
    .out_7(n4_bit_asynchronous_down_counter_3_out_7), .out_8(n4_bit_asynchronous_down_counter_3_out_8),
    .Disable(display_product_1_p7));
  and and_5 (and_5_out, C__6, n4_bit_asynchronous_down_counter_3_out_8);
  and and_6 (and_6_out, D__8, n4_bit_asynchronous_down_counter_4_out_8);
  _4_bit_Asynchronous_Down_Counter u_4_bit_asynchronous_down_counter_4 (
    .Clock(and_3_out), .Preset(Restock_D), .out_4(n4_bit_asynchronous_down_counter_4_out_4),
    .out_5(n4_bit_asynchronous_down_counter_4_out_5), .out_6(n4_bit_asynchronous_down_counter_4_out_6),
    .out_7(n4_bit_asynchronous_down_counter_4_out_7), .out_8(n4_bit_asynchronous_down_counter_4_out_8),
    .Disable(display_product_1_p5));
  or or_1 (or_1_out, and_1_out, and_3_out);
  and and_7 (and_7_out, E__12, n4_bit_asynchronous_down_counter_5_out_8);
  _4_bit_Asynchronous_Down_Counter u_4_bit_asynchronous_down_counter_5 (
    .Clock(and_3_out), .Preset(Restock_E), .out_4(n4_bit_asynchronous_down_counter_5_out_4),
    .out_5(n4_bit_asynchronous_down_counter_5_out_5), .out_6(n4_bit_asynchronous_down_counter_5_out_6),
    .out_7(n4_bit_asynchronous_down_counter_5_out_7), .out_8(n4_bit_asynchronous_down_counter_5_out_8),
    .Disable(display_product_1_p2));
  Insert_Money insert_money_1 (
    ._1(_1), ._2(_2), ._5(_5), ._10(_10), .out_7(insert_money_1_out_7), .out_8(insert_money_1_out_8),
    .out_9(insert_money_1_out_9), .out_10(insert_money_1_out_10), .Clear(or_1_out),
    .Disable(display_product_1_p14));
  Product_Selection product_selection_1 (
    .out_8(product_selection_1_out_8), .out_9(product_selection_1_out_9),
    .out_10(product_selection_1_out_10), .out_11(product_selection_1_out_11), ._2(and_2_out), ._3(and_4_out),
    ._6(and_5_out), ._8(and_6_out), ._12(and_7_out), .Clear(or_1_out), .Disable(display_product_1_p14));
  _4_bit_binary_to_7_segment_display u_4_bit_binary_to_7_segment_display_1 (
    .in_1(n4_bit_asynchronous_down_counter_1_out_7), .in_3(n4_bit_asynchronous_down_counter_1_out_6),
    .in_4(n4_bit_asynchronous_down_counter_1_out_5), .in_5(n4_bit_asynchronous_down_counter_1_out_4),
    .out_6(out_27), .out_7(out_28), .out_11(out_26), .out_12(out_25), .in_2(1'b1));  // open: out_8, out_9, out_10, out_13, out_14, out_15, out_16, out_17, out_18, out_19
  _4_bit_binary_to_7_segment_display u_4_bit_binary_to_7_segment_display_2 (
    .in_1(n4_bit_asynchronous_down_counter_2_out_7), .in_3(n4_bit_asynchronous_down_counter_2_out_6),
    .in_4(n4_bit_asynchronous_down_counter_2_out_5), .in_5(n4_bit_asynchronous_down_counter_2_out_4),
    .out_6(out_31), .out_7(out_32), .out_11(out_30), .out_12(out_29), .in_2(1'b1));  // open: out_8, out_9, out_10, out_13, out_14, out_15, out_16, out_17, out_18, out_19
  _4_bit_binary_to_7_segment_display u_4_bit_binary_to_7_segment_display_3 (
    .in_1(n4_bit_asynchronous_down_counter_3_out_7), .in_3(n4_bit_asynchronous_down_counter_3_out_6),
    .in_4(n4_bit_asynchronous_down_counter_3_out_5), .in_5(n4_bit_asynchronous_down_counter_3_out_4),
    .out_6(out_35), .out_7(out_36), .out_11(out_34), .out_12(out_33), .in_2(1'b1));  // open: out_8, out_9, out_10, out_13, out_14, out_15, out_16, out_17, out_18, out_19
  _4_bit_binary_to_7_segment_display u_4_bit_binary_to_7_segment_display_4 (
    .in_1(n4_bit_asynchronous_down_counter_4_out_7), .in_3(n4_bit_asynchronous_down_counter_4_out_6),
    .in_4(n4_bit_asynchronous_down_counter_4_out_5), .in_5(n4_bit_asynchronous_down_counter_4_out_4),
    .out_6(out_47), .out_7(out_48), .out_11(out_46), .out_12(out_45), .in_2(1'b1));  // open: out_8, out_9, out_10, out_13, out_14, out_15, out_16, out_17, out_18, out_19
  _4_bit_binary_to_7_segment_display u_4_bit_binary_to_7_segment_display_5 (
    .in_1(n4_bit_asynchronous_down_counter_5_out_7), .in_3(n4_bit_asynchronous_down_counter_5_out_6),
    .in_4(n4_bit_asynchronous_down_counter_5_out_5), .in_5(n4_bit_asynchronous_down_counter_5_out_4),
    .out_6(out_51), .out_7(out_52), .out_11(out_50), .out_12(out_49), .in_2(1'b1));  // open: out_8, out_9, out_10, out_13, out_14, out_15, out_16, out_17, out_18, out_19
  // Display_Product display_product_1: pin names not known; wires that end beside it: product_selection_1_out_8, display_product_1_p2, product_selection_1_out_9, out_37, display_product_1_p5, out_38, display_product_1_p7, product_selection_1_out_10, out_39, display_product_1_p10, out_40, display_product_1_p12, product_selection_1_out_11, display_product_1_p14
  or or_2 (or_2_out, product_selection_1_out_8, product_selection_1_out_9, product_selection_1_out_10, product_selection_1_out_11);
  Calculation calculation_1 (
    .in_5(product_selection_1_out_8), .Price(product_selection_1_out_9), .in_7(product_selection_1_out_10),
    .in_8(product_selection_1_out_11), .out_9(calculation_1_out_9), .out_10(calculation_1_out_10),
    .out_11(calculation_1_out_11), .out_12(calculation_1_out_12), .out_13(calculation_1_out_13),
    .in_1(insert_money_1_out_7), .Money(insert_money_1_out_8), .in_3(insert_money_1_out_9),
    .in_4(insert_money_1_out_10));
  and and_8 (display_product_1_p14, or_2_out, calculation_1_out_9);
  not not_1 (not_1_out, calculation_1_out_9);
  not not_2 (not_2_out, display_product_1_p14);
  _4_bit_binary_to_7_segment_display u_4_bit_binary_to_7_segment_display_6 (
    .in_1(insert_money_1_out_7), .in_3(insert_money_1_out_8), .in_4(insert_money_1_out_9),
    .in_5(insert_money_1_out_10), .out_6(out_19), .out_7(out_20), .out_11(out_18), .out_12(out_17),
    .in_2(not_2_out));  // open: out_8, out_9, out_10, out_13, out_14, out_15, out_16, out_17, out_18, out_19
  _4_bit_binary_to_7_segment_display u_4_bit_binary_to_7_segment_display_7 (
    .in_1(calculation_1_out_10), .in_3(calculation_1_out_11), .in_4(calculation_1_out_12),
    .in_5(calculation_1_out_13), .out_6(out_23), .out_7(out_24), .out_11(out_22), .out_12(out_21),
    .in_2(not_1_out));  // open: out_8, out_9, out_10, out_13, out_14, out_15, out_16, out_17, out_18, out_19
  _4_bit_binary_to_7_segment_display u_4_bit_binary_to_7_segment_display_8 (
    .in_1(calculation_1_out_10), .in_3(calculation_1_out_11), .in_4(calculation_1_out_12),
    .in_5(calculation_1_out_13), .out_6(out_43), .out_7(out_44), .out_11(out_42), .out_12(out_41),
    .in_2(display_product_1_p14));  // open: out_8, out_9, out_10, out_13, out_14, out_15, out_16, out_17, out_18, out_19

  // Notes on the sheet:
  //   Product
  //   Dollar
  //   Inserted
  //   Dollar
  //   Needed
  //   Return
endmodule

module Insert_Money (
  input  Clear,
  input  Disable,
  input  _1,
  input  _2,
  input  _5,
  input  _10,
  output out_7,
  output out_8,
  output out_9,
  output out_10
);

  wire LSB_out, n4_bit_adder_subtractor_1_out_10, n4_bit_adder_subtractor_1_out_11,
       n4_bit_adder_subtractor_1_out_12, n4_bit_adder_subtractor_1_out_13, n4_bit_adder_subtractor_1_out_14,
       nor_1_out, or_1_out, or_2_out;

  or or_1 (or_1_out, _10, _2);
  or LSB (LSB_out, _5, _1);
  nor nor_1 (nor_1_out, _10, _5, _2, _1);
  _4_Bit_Adder_Subtractor u_4_bit_adder_subtractor_1 (
    .in_1(1'b0), .in_2(_10), .in_3(out_7), .in_4(_5), .in_5(out_8), .in_6(or_1_out), .in_7(out_9),
    .in_8(LSB_out), .in_9(out_10), .out_10(n4_bit_adder_subtractor_1_out_10),
    .out_11(n4_bit_adder_subtractor_1_out_11), .out_12(n4_bit_adder_subtractor_1_out_12),
    .out_13(n4_bit_adder_subtractor_1_out_13), .out_14(n4_bit_adder_subtractor_1_out_14));
  _4_bit_memory u_4_bit_memory_1 (
    .in_3(n4_bit_adder_subtractor_1_out_11), .in_4(n4_bit_adder_subtractor_1_out_12),
    .in_5(n4_bit_adder_subtractor_1_out_13), .in_6(n4_bit_adder_subtractor_1_out_14), .out_8(out_7),
    .out_9(out_8), .out_10(out_9), .out_11(out_10), .Clear(Clear), .Clk(nor_1_out), .Disabled(or_2_out));
  or or_2 (or_2_out, n4_bit_adder_subtractor_1_out_10, Disable);
endmodule

module _4_bit_binary_to_7_segment_display (
  input  in_1,
  input  in_2,
  input  in_3,
  input  in_4,
  input  in_5,
  output out_6,
  output out_7,
  output out_8,
  output out_9,
  output out_10,
  output out_11,
  output out_12,
  output out_13,
  output out_14,
  output out_15,
  output out_16,
  output out_17,
  output out_18,
  output out_19
);

  wire _0_out, _1_out, _2_out, _3_out, _4_out, _5_out, _6_out, _7_out, _8_out, _10_out, _11_out, _12_out,
       _13_out, _14_out, _15_out, nor_1_out, nor_2_out, nor_3_out, nor_4_out, nor_5_out, nor_6_out,
       nor_7_out, not_1_out, not_2_out, not_3_out, not_4_out, or_1_out;

  not not_1 (not_1_out, in_1);
  not not_2 (not_2_out, in_3);
  not not_3 (not_3_out, in_4);
  not not_4 (not_4_out, in_5);
  and _0 (_0_out, not_1_out, not_2_out, not_3_out, not_4_out);
  and _1 (_1_out, not_1_out, not_2_out, not_3_out, in_5);
  and _2 (_2_out, not_1_out, not_2_out, in_4, not_4_out);
  and _3 (_3_out, not_1_out, not_2_out, in_4, in_5);
  and _4 (_4_out, not_1_out, in_3, not_3_out, not_4_out);
  and _5 (_5_out, not_1_out, in_3, not_3_out, in_5);
  and _6 (_6_out, not_1_out, in_3, in_4, not_4_out);
  and _7 (_7_out, not_1_out, in_3, in_4, in_5);
  and _8 (_8_out, in_1, not_2_out, not_3_out, not_4_out);
  // AND_Gate _9 has open pins: in0=in_1, in1=not_2_out, in2=not_3_out, in3=in_5, out=open
  and _10 (_10_out, in_1, not_2_out, in_4, not_4_out);
  and _11 (_11_out, in_1, not_2_out, in_4, in_5);
  and _12 (_12_out, in_1, in_3, not_3_out, not_4_out);
  and _13 (_13_out, in_1, in_3, not_3_out, in_5);
  and _14 (_14_out, in_1, in_3, in_4, not_4_out);
  and _15 (_15_out, in_1, in_3, in_4, in_5);
  or or_1 (or_1_out, _12_out, _10_out, _8_out, _6_out, _2_out, _0_out);
  nor nor_1 (nor_1_out, _15_out, _14_out, _13_out, _12_out, _11_out, _10_out);
  nor nor_2 (nor_2_out, _14_out, _11_out, _4_out, _1_out);
  nor nor_3 (nor_3_out, _15_out, _6_out, _5_out);
  nor nor_4 (nor_4_out, _12_out, _2_out);
  nor nor_5 (nor_5_out, _14_out, _11_out, _7_out, _4_out, _1_out);
  nor nor_6 (nor_6_out, _13_out, _12_out, _11_out, _7_out, _3_out, _2_out, _1_out);
  nor nor_7 (nor_7_out, _11_out, _10_out, _7_out, _1_out, _0_out);
  and and_1 (out_6, in_2, nor_1_out);
  and and_2 (out_7, in_2, 1'b1);
  and and_3 (out_8, in_2, 1'b1);
  and and_4 (out_9, in_2, nor_1_out);
  and and_5 (out_10, in_2, nor_1_out);
  and and_6 (out_11, in_2, nor_1_out);
  and and_7 (out_12, in_2, 1'b0);
  and and_8 (out_13, in_2, nor_2_out);
  and and_9 (out_14, in_2, nor_3_out);
  and and_10 (out_15, in_2, nor_4_out);
  and and_11 (out_16, in_2, nor_5_out);
  and and_12 (out_17, in_2, or_1_out);
  and and_13 (out_18, in_2, nor_6_out);
  and and_14 (out_19, in_2, nor_7_out);
endmodule

module Product_Selection (
  input  Disable,
  input  _2,
  input  _3,
  input  _6,
  input  _8,
  input  _12,
  input  Clear,
  output out_8,
  output out_9,
  output out_10,
  output out_11
);

  wire MSB_out, or_1_out, or_2_out, or_3_out;

  or MSB (MSB_out, _12, _8);
  or or_1 (or_1_out, _12, _6);
  or or_2 (or_2_out, _6, _3, _2);
  or or_3 (or_3_out, _12, _8, _6, _3, _2);
  _4_bit_memory u_4_bit_memory_1 (
    .in_3(MSB_out), .in_4(or_1_out), .in_5(or_2_out), .in_6(_3), .out_8(out_8), .out_9(out_9),
    .out_10(out_10), .out_11(out_11), .Clear(Clear), .Clk(or_3_out), .Disabled(Disable));
endmodule

module _4_Bit_Comparator (
  input  A,
  input  B,
  input  A_2,
  input  B_2,
  input  A_3,
  input  B_3,
  input  A_4,
  input  B_4,
  output out_9
);

  wire A_B_out, and_1_out, and_2_out, and_3_out, and_4_out, and_5_out, and_6_out, and_7_out, and_8_out,
       and_9_out, and_10_out, and_11_out, and_12_out, nor_1_out, nor_2_out, nor_3_out, nor_4_out, not_1_out,
       not_2_out, not_3_out, not_4_out, not_5_out, not_6_out, not_7_out, not_8_out;

  not not_1 (not_1_out, A);
  not not_2 (not_2_out, B);
  not not_3 (not_3_out, A_2);
  not not_4 (not_4_out, B_2);
  not not_5 (not_5_out, A_3);
  not not_6 (not_6_out, B_3);
  not not_7 (not_7_out, A_4);
  not not_8 (not_8_out, B_4);
  and and_1 (and_1_out, not_1_out, B);
  and and_2 (and_2_out, A, not_2_out);
  and and_3 (and_3_out, not_3_out, B_2);
  and and_4 (and_4_out, A_2, not_4_out);
  and and_5 (and_5_out, not_5_out, B_3);
  and and_6 (and_6_out, A_3, not_6_out);
  and and_7 (and_7_out, not_7_out, B_4);
  and and_8 (and_8_out, A_4, not_8_out);
  nor nor_1 (nor_1_out, and_1_out, and_2_out);
  nor nor_2 (nor_2_out, and_3_out, and_4_out);
  nor nor_3 (nor_3_out, and_5_out, and_6_out);
  nor nor_4 (nor_4_out, and_7_out, and_8_out);
  and and_9 (and_9_out, nor_1_out, and_4_out);
  and and_10 (and_10_out, nor_1_out, nor_2_out, and_6_out);
  and and_11 (and_11_out, nor_1_out, nor_2_out, nor_3_out, and_8_out);
  and and_12 (and_12_out, nor_1_out, nor_2_out, nor_3_out, nor_4_out);
  or A_B (A_B_out, and_2_out, and_9_out, and_10_out, and_11_out);
  or A__B (out_9, A_B_out, and_12_out);

  // Notes on the sheet:
  //   MSB
  //   LSB
endmodule

module _4_Bit_Adder_Subtractor (
  input  in_1,
  input  in_2,
  input  in_3,
  input  in_4,
  input  in_5,
  input  in_6,
  input  in_7,
  input  in_8,
  input  in_9,
  output out_10,
  output out_11,
  output out_12,
  output out_13,
  output out_14
);

  wire adder_2_cout, adder_3_cout, adder_4_cout, xor_1_out, xor_2_out, xor_3_out, xor_4_out;

  xor xor_1 (xor_1_out, in_1, in_3);
  xor xor_2 (xor_2_out, in_1, in_5);
  xor xor_3 (xor_3_out, in_1, in_7);
  xor xor_4 (xor_4_out, in_1, in_9);
  Adder #(.width(1)) adder_1 (.a(in_2), .b(xor_1_out), .out(out_11), .cin(adder_2_cout), .cout(out_10));
  Adder #(.width(1)) adder_2 (.a(in_4), .b(xor_2_out), .out(out_12), .cin(adder_3_cout), .cout(adder_2_cout));
  Adder #(.width(1)) adder_3 (.a(in_6), .b(xor_3_out), .out(out_13), .cin(adder_4_cout), .cout(adder_3_cout));
  Adder #(.width(1)) adder_4 (.a(in_8), .b(xor_4_out), .out(out_14), .cin(in_1), .cout(adder_4_cout));
endmodule

module _4_bit_memory (
  input  Disabled,
  input  Clear,
  input  in_3,
  input  in_4,
  input  in_5,
  input  in_6,
  input  Clk,
  output out_8,
  output out_9,
  output out_10,
  output out_11
);

  wire not_1_out;

  not not_1 (not_1_out, Disabled);
  D_Flip_Flop d_ff_1 (.clk(Clk), .D(in_3), .Q(out_8), .en(not_1_out), .reset(Clear));  // open: Qn, preset
  D_Flip_Flop d_ff_2 (.clk(Clk), .D(in_4), .Q(out_9), .en(not_1_out), .reset(Clear));  // open: Qn, preset
  D_Flip_Flop d_ff_3 (.clk(Clk), .D(in_5), .Q(out_10), .en(not_1_out), .reset(Clear));  // open: Qn, preset
  D_Flip_Flop d_ff_4 (.clk(Clk), .D(in_6), .Q(out_11), .en(not_1_out), .reset(Clear));  // open: Qn, preset
endmodule

module Calculation (
  input  in_1,
  input  Money,
  input  in_3,
  input  in_4,
  input  in_5,
  input  Price,
  input  in_7,
  input  in_8,
  output out_9,
  output out_10,
  output out_11,
  output out_12,
  output out_13
);

  wire n4_bit_adder_subtractor_1_out_10, n4_bit_adder_subtractor_1_out_11, n4_bit_adder_subtractor_1_out_12,
       n4_bit_adder_subtractor_1_out_13, n4_bit_adder_subtractor_1_out_14, not_1_out, not_2_out;

  _4_Bit_Comparator u_4_bit_comparator_1 (
    .A(in_1), .B(in_5), .A_2(Money), .B_2(Price), .A_3(in_3), .B_3(in_7), .A_4(in_4), .B_4(in_8),
    .out_9(out_9));
  _4_Bit_Adder_Subtractor u_4_bit_adder_subtractor_1 (
    .in_1(1'b1), .in_2(in_1), .in_3(in_5), .in_4(Money), .in_5(Price), .in_6(in_3), .in_7(in_7), .in_8(in_4),
    .in_9(in_8), .out_10(n4_bit_adder_subtractor_1_out_10), .out_11(n4_bit_adder_subtractor_1_out_11),
    .out_12(n4_bit_adder_subtractor_1_out_12), .out_13(n4_bit_adder_subtractor_1_out_13),
    .out_14(n4_bit_adder_subtractor_1_out_14));
  not not_1 (not_1_out, 1'b1);
  _4_Bit_Adder_Subtractor u_4_bit_adder_subtractor_2 (
    .in_1(not_2_out), .in_2(not_1_out), .in_3(n4_bit_adder_subtractor_1_out_11), .in_4(not_1_out),
    .in_5(n4_bit_adder_subtractor_1_out_12), .in_6(not_1_out), .in_7(n4_bit_adder_subtractor_1_out_13),
    .in_8(not_1_out), .in_9(n4_bit_adder_subtractor_1_out_14), .out_11(out_10), .out_12(out_11),
    .out_13(out_12), .out_14(out_13));  // open: out_10
  not not_2 (not_2_out, n4_bit_adder_subtractor_1_out_10);
endmodule

module Display_Product (
  input  in_1,
  input  in_2,
  input  in_3,
  input  in_4,
  input  in_5,
  output out_6,
  output out_7,
  output out_8,
  output out_9,
  output out_10,
  output out_11,
  output out_12,
  output out_13,
  output out_14,
  output out_15,
  output out_16,
  output out_17
);

  wire nor_1_out, nor_2_out, not_1_out, not_2_out, not_3_out, not_4_out, not_5_out;

  not not_1 (not_1_out, in_1);
  not not_2 (not_2_out, in_3);
  not not_3 (not_3_out, in_4);
  not not_4 (not_4_out, in_5);
  and _2 (out_13, not_1_out, not_2_out, in_4, not_4_out);
  and _6 (out_15, not_1_out, in_3, in_4, not_4_out);
  and _3 (out_14, not_1_out, not_2_out, in_4, in_5);
  and _8 (out_16, in_1, not_2_out, not_3_out, not_4_out);
  and _12 (out_17, in_1, in_3, not_3_out, not_4_out);
  nor nor_1 (nor_1_out, out_17, out_15);
  not not_5 (not_5_out, out_13);
  nor nor_2 (nor_2_out, out_16, out_15);
  and and_1 (out_7, in_2, nor_1_out);
  and and_2 (out_8, in_2, nor_1_out);
  and and_3 (out_9, in_2, not_5_out);
  and and_4 (out_12, in_2, nor_2_out);

  assign out_6 = in_2;
  assign out_10 = in_2;
  assign out_11 = in_2;
endmodule

module Digital_Vending_Machine (
);

  Button Restock_A ();  // open: out
  Button Restock_B ();  // open: out
  Button Restock_C ();  // open: out
  Button Restock_D ();  // open: out
  Button Restock_E ();  // open: out
  Button _1 ();  // open: out
  Button _2 ();  // open: out
  Button _5 ();  // open: out
  Button _10 ();  // open: out
  Button A__2 ();  // open: out
  Button B__3 ();  // open: out
  Button C__6 ();  // open: out
  Button D__8 ();  // open: out
  Button E__12 ();  // open: out
  Button Cancel ();  // open: out
  Button Take_Return___Product ();  // open: out
  _7_Segment_Display u_7_segment_display_1 ();  // open: g, f, a, b, e, d, c, dp
  _7_Segment_Display u_7_segment_display_2 ();  // open: g, f, a, b, e, d, c, dp
  _7_Segment_Display u_7_segment_display_3 ();  // open: g, f, a, b, e, d, c, dp
  _7_Segment_Display u_7_segment_display_4 ();  // open: g, f, a, b, e, d, c, dp
  _7_Segment_Display u_7_segment_display_5 ();  // open: g, f, a, b, e, d, c, dp
  _7_Segment_Display u_7_segment_display_6 ();  // open: g, f, a, b, e, d, c, dp
  _7_Segment_Display u_7_segment_display_7 ();  // open: g, f, a, b, e, d, c, dp
  _7_Segment_Display u_7_segment_display_8 ();  // open: g, f, a, b, e, d, c, dp
  _7_Segment_Display u_7_segment_display_9 ();  // open: g, f, a, b, e, d, c, dp
  _7_Segment_Display u_7_segment_display_10 ();  // open: g, f, a, b, e, d, c, dp
  _7_Segment_Display u_7_segment_display_11 ();  // open: g, f, a, b, e, d, c, dp
  _7_Segment_Display u_7_segment_display_12 ();  // open: g, f, a, b, e, d, c, dp
  _7_Segment_Display u_7_segment_display_13 ();  // open: g, f, a, b, e, d, c, dp
  _7_Segment_Display u_7_segment_display_14 ();  // open: g, f, a, b, e, d, c, dp
  _7_Segment_Display u_7_segment_display_15 ();  // open: g, f, a, b, e, d, c, dp
  _7_Segment_Display u_7_segment_display_16 ();  // open: g, f, a, b, e, d, c, dp
  _7_Segment_Display u_7_segment_display_17 ();  // open: g, f, a, b, e, d, c, dp
endmodule

module _4_bit_Asynchronous_Down_Counter (
  input  Clock,
  input  Preset,
  input  Disable,
  output out_4,
  output out_5,
  output out_6,
  output out_7,
  output out_8
);

  wire and_1_out;

  T_Flip_Flop t_ff_1 (.clk(Clock), .T(1'b1), .Q(out_4), .preset(Preset), .en(and_1_out));  // open: Qn, reset
  T_Flip_Flop t_ff_2 (.clk(out_4), .T(1'b1), .Q(out_5), .preset(Preset), .en(and_1_out));  // open: Qn, reset
  T_Flip_Flop t_ff_3 (.clk(out_5), .T(1'b1), .Q(out_6), .preset(Preset), .en(and_1_out));  // open: Qn, reset
  T_Flip_Flop t_ff_4 (.clk(out_6), .T(1'b1), .Q(out_7), .preset(Preset), .en(and_1_out));  // open: Qn, reset
  and and_1 (and_1_out, Disable, out_8);
  or or_1 (out_8, out_4, out_5, out_6, out_7);
endmodule
